# Fritzing sketch Schematics (saved by Fritzing 0.9.6b)
breadboards: 1

parts:
  Gizwits_WiFi_Witty_ESP-12F1 = Gizwits WiFi Witty ESP-12F
  R1 = Resistor [tolerance=±5% resistance=10k package="0805 [SMD]"]
  R2 = Resistor [tolerance=±5% resistance=10k package="0805 [SMD]"]
  R3 = Resistor [tolerance=±5% resistance=10k package="0805 [SMD]"]
  R4 = Resistor [tolerance=±5% resistance=10k package="0805 [SMD]"]
  Reset = SWITCH-MOMENTARY-2 [package=tactile-pth-12mm]
  Flash = SWITCH-MOMENTARY-2 [package=tactile-pth-12mm]
  Programmer = Camdenboss CTB0158-3 [part_number=CTB0158-3 package=THT]
  U2 = Vibration Motor- ROB-08449 [package=vibe-motor-10mm]
  Q1 = TRANSISTOR_NPN [part_number=c945 package=to-92-ammo]
  R9 = Resistor [tolerance=±5% resistance=330 package="0805 [SMD]"]
  D1 = Diode [package=diode-1n4001]
  R10 = Resistor [tolerance=±5% resistance=27k package="0805 [SMD]"]
  R11 = Resistor [tolerance=±5% resistance=100k package="0805 [SMD]"]
  Q2 = TRANSISTOR_NPN [part_number=c945 package=to-92-ammo]
  FSR = VARISTOR [package=0402-res]
  R12 = Resistor [tolerance=±5% resistance=33k package="0805 [SMD]"]
  U3 = Voltage Regulator - 3.3V [part_number=MCP1700-3302E package="TO220 [THT]"]
  X1 = USB Connectors [package=usb-a-s]
  M1 = TP4056 Module [part_number=HW-107]
  Li-Po_~_4_2V = LIPO-1000mAh [package=lipo-1000]
  C1 = Capacitor [part_number=100nF package=cap-pth-small2]
  C2 = Capacitor Polarized [part_number=100uF package=panasonic_e]
  S1 = SPST Switch [part_number="SPDT switch" package=ayz0202]
  R13 = Resistor [tolerance=±5% resistance=330 package="0805 [SMD]"]

nets:
  N1: Gizwits_WiFi_Witty_ESP-12F1.REST, R3.Pin_1, Reset.2
  N2: Gizwits_WiFi_Witty_ESP-12F1.ADC, D1.C, Q2.E
  N3: Gizwits_WiFi_Witty_ESP-12F1.CH_PD, R4.Pin_1
  N4: Gizwits_WiFi_Witty_ESP-12F1.GPIO14, R9.Pin_0
  N5: Gizwits_WiFi_Witty_ESP-12F1.VCC, R2.Pin_1
  GND: Gizwits_WiFi_Witty_ESP-12F1.GND, R1.Pin_0, Reset.1, Flash.1, Programmer.pin3, Q1.E, R11.Pin_1, R12.Pin_1, U3.GND, M1.OUT-#1, C1.2, C2.-
  N6: Gizwits_WiFi_Witty_ESP-12F1.GPIO15, R1.Pin_1
  N7: Gizwits_WiFi_Witty_ESP-12F1.GPIO0, R2.Pin_0, Flash.2
  N8: Gizwits_WiFi_Witty_ESP-12F1.GPIO4, FSR.1
  N9: Gizwits_WiFi_Witty_ESP-12F1.GPIO5, R13.Pin_0
  N10: Gizwits_WiFi_Witty_ESP-12F1.RXD, Programmer.pin2
  N11: Gizwits_WiFi_Witty_ESP-12F1.TXD, Programmer.pin1
  N12: R3.Pin_0, U2.+
  N13: R4.Pin_0, U3.output_voltage, C1.1, C2.+
  N14: U2.-, Q1.C
  N15: Q1.B, R9.Pin_1
  N16: D1.A, FSR.2, R12.Pin_0
  N17: R10.Pin_0, U3.input_voltage, S1.O
  N18: R10.Pin_1, R11.Pin_0, Q2.C
  N19: Q2.B, R13.Pin_1
  N20: X1.D+, M1.VCC
  GND_2: X1.GND, M1.GND
  N21: M1.BAT-, Li-Po_~_4_2V.-
  N22: M1.BAT+, Li-Po_~_4_2V.+
  N23: M1.OUT-#4, S1.P

custom parts:
  TP4056 Module: TP4056 Lithium Battery Charge Management Module Links: TP4056 website
