# Fritzing sketch SchematicsDigitalSensor (saved by Fritzing 0.9.6b)
breadboards: 1

parts:
  Gizwits_WiFi_Witty_ESP-12F1 = Gizwits WiFi Witty ESP-12F
  R1 = Resistor [tolerance=±5% resistance=10k package="0805 [SMD]"]
  R2 = Resistor [tolerance=±5% resistance=10k package="0805 [SMD]"]
  R3 = Resistor [tolerance=±5% resistance=10k package="0805 [SMD]"]
  R4 = Resistor [tolerance=±5% resistance=10k package="0805 [SMD]"]
  Reset = SWITCH-MOMENTARY-2 [package=tactile-pth-12mm]
  Flash = SWITCH-MOMENTARY-2 [package=tactile-pth-12mm]
  Programmer = Camdenboss CTB0158-3 [part_number=CTB0158-3 package=THT]
  U2 = Vibration Motor- ROB-08449 [package=vibe-motor-10mm]
  Q1 = TRANSISTOR_NPN [part_number=c945 package=to-92-ammo]
  R9 = Resistor [tolerance=±5% resistance=1k package="0805 [SMD]"]
  R10 = Resistor [tolerance=±5% resistance=27k package="0805 [SMD]"]
  R11 = Resistor [tolerance=±5% resistance=100k package="0805 [SMD]"]
  U3 = Voltage Regulator - 3.3V [part_number=MCP1700-3302E package="TO220 [THT]"]
  C1 = Capacitor [part_number=100nF package=cap-pth-small2]
  C2 = Capacitor Polarized [part_number=100uF package=panasonic_e]
  S1 = SPST Switch [part_number="SPDT switch" package=ayz0202]
  Sensor = SWITCH-MOMENTARY-2 [package=tactile-pth-12mm]
  X2 = USB Connectors [package=usb-a-s]
  M3 = TP4056 Module [part_number=HW-107]
  U5 = LIPO-1000mAh [package=lipo-1000]
  R12 = Resistor [tolerance=±5% resistance=330 package="0805 [SMD]"]

nets:
  N1: Gizwits_WiFi_Witty_ESP-12F1.REST, R3.Pin_1, Reset.2
  N2: Gizwits_WiFi_Witty_ESP-12F1.ADC, R10.Pin_1, R11.Pin_0
  N3: Gizwits_WiFi_Witty_ESP-12F1.CH_PD, R4.Pin_1
  N4: Gizwits_WiFi_Witty_ESP-12F1.VCC, R2.Pin_1, R3.Pin_0, R4.Pin_0, U3.output_voltage, C1.1, C2.+, R12.Pin_0
  GND: Gizwits_WiFi_Witty_ESP-12F1.GND, R1.Pin_0, Reset.1, Flash.1, Programmer.pin3, Q1.E, R11.Pin_1, U3.GND, C1.2, C2.-, Sensor.1, M3.OUT-#1
  N5: Gizwits_WiFi_Witty_ESP-12F1.GPIO15, R1.Pin_1
  N6: Gizwits_WiFi_Witty_ESP-12F1.GPIO0, R2.Pin_0, Flash.2
  N7: Gizwits_WiFi_Witty_ESP-12F1.GPIO4, R9.Pin_0
  N8: Gizwits_WiFi_Witty_ESP-12F1.GPIO5, Sensor.2
  N9: Gizwits_WiFi_Witty_ESP-12F1.RXD, Programmer.pin2
  N10: Gizwits_WiFi_Witty_ESP-12F1.TXD, Programmer.pin1
  N11: U2.+, R12.Pin_1
  N12: U2.-, Q1.C
  N13: Q1.B, R9.Pin_1
  N14: R10.Pin_0, U3.input_voltage, S1.O
  N15: S1.P, M3.OUT-#4
  N16: X2.D+, M3.VCC
  GND_2: X2.GND, M3.GND
  N17: M3.BAT-, U5.-
  N18: M3.BAT+, U5.+

custom parts:
  TP4056 Module: TP4056 Lithium Battery Charge Management Module Links: TP4056 website
